# Fritzing sketch motionTrackerThing (saved by Fritzing 0.9.3b)
breadboards: 1

parts:
  Part1 = Arduino Nano (Rev3.0)
  Part2 = Bluetooth HC-05 Macho
  LED1 = smd LED [color="Red (633nm)" package="0805 [SMD]"]
  GY2 = MPU-6050 Board GY-521 [form="♀ (female)" package=THT]
  BAT1 = BC9VPC [package=bc9vpc]

nets:
  N1: Part1.D1/TX, Part2.RXD
  N2: Part1.D0/RX, Part2.TXD
  GND: Part1.GND, Part2.GND, LED1.anode, GY2.pin2, BAT1.V-
  N3: Part1.D2, GY2.pin8
  N4: Part1.D3, LED1.cathode
  N5: Part1.VIN, BAT1.V+
  5V: Part1.5V, Part2.VCC, GY2.pin1
  N6: Part1.A5, GY2.pin3
  N7: Part1.A4, GY2.pin4

custom parts:
  MPU-6050 Board GY-521: Acelerometro y Giroscopio MPU-6050 Board GY-521
